// Logisim project F2.circ as structural Verilog: 1 circuit, main circuit main
module main (
  input  A,
  input  B,
  input  C,
  input  D,
  output out_5
);

  wire and_1_out, and_2_out, and_3_out, not_1_out;

  not not_1 (not_1_out, B);
  and and_1 (and_1_out, A, not_1_out);
  and and_2 (and_2_out, C, D);
  and and_3 (and_3_out, B, D);
  or or_1 (out_5, and_1_out, and_2_out, and_3_out);
endmodule
