// Logisim project F2_with_nand_gate.circ as structural Verilog: 1 circuit, main circuit main
module main (
  input  A,
  input  B,
  input  C,
  input  D,
  output out_5
);

  wire nand_1_out, nand_2_out, nand_3_out, nand_4_out;

  nand nand_1 (nand_1_out, B, B);
  nand nand_2 (nand_2_out, A, nand_1_out);
  nand nand_3 (nand_3_out, C, D);
  nand nand_4 (nand_4_out, B, D);
  nand nand_5 (out_5, nand_2_out, nand_3_out, nand_4_out);
endmodule
