// Logisim project neg_F_with_nand.circ as structural Verilog: 1 circuit, main circuit main
module main (
  input  A,
  input  B,
  input  C,
  input  D,
  output out_5
);

  wire nand_1_out, nand_2_out, nand_3_out, nand_4_out, nand_5_out, nand_6_out, nand_7_out;

  nand nand_1 (nand_1_out, A, A);
  nand nand_2 (nand_2_out, B, B);
  nand nand_3 (nand_3_out, C, C);
  nand nand_4 (nand_4_out, D, D);
  nand nand_5 (nand_5_out, nand_1_out, nand_2_out, D);
  nand nand_6 (nand_6_out, nand_1_out, nand_3_out, D);
  nand nand_7 (nand_7_out, B, nand_3_out, nand_4_out);
  nand nand_8 (out_5, nand_5_out, nand_6_out, nand_7_out);
endmodule
