// Logisim project CSE232_Hw3.circ as structural Verilog: 1 circuit, main circuit main
module main (
  input  a,
  input  in_2,
  output x,
  output y,
  output z
);

  wire and_1_out, and_2_out, and_3_out, and_4_out, and_5_out, and_6_out, and_7_out, and_8_out, and_9_out,
       and_10_out, and_11_out, and_12_out, and_13_out, and_14_out, and_15_out, and_16_out, and_17_out,
       clock_1_out, not_1_out, not_2_out, not_3_out, not_4_out, not_5_out, not_6_out, not_7_out, not_8_out,
       not_9_out, not_10_out, not_11_out, not_12_out, not_13_out, not_14_out, not_15_out, not_16_out,
       not_17_out, not_18_out, not_19_out, not_20_out, not_21_out, not_22_out, or_1_out, or_2_out, or_3_out,
       s0_q, s1_q, s2_q;

  Clock clock_1 (.out(clock_1_out));
  not not_1 (not_1_out, s1_q);
  not not_2 (not_2_out, s0_q);
  not not_3 (not_3_out, a);
  and and_1 (and_1_out, s2_q, not_1_out);
  and and_2 (and_2_out, s2_q, not_2_out, not_3_out);
  and and_3 (and_3_out, s1_q, s0_q, a);
  Register #(.width(1)) s2 (.D(or_1_out), .en(in_2), .Q(s2_q), .clk(clock_1_out));  // open: clr
  or or_1 (or_1_out, and_1_out, and_2_out, and_3_out);
  Register #(.width(1)) s1 (.D(or_2_out), .en(in_2), .Q(s1_q), .clk(clock_1_out));  // open: clr
  not not_4 (not_4_out, s1_q);
  and and_4 (and_4_out, not_4_out, s0_q, a);
  not not_5 (not_5_out, s2_q);
  and and_5 (and_5_out, not_5_out, s1_q, not_6_out);
  not not_6 (not_6_out, s0_q);
  not not_7 (not_7_out, s0_q);
  and and_6 (and_6_out, s1_q, not_7_out, not_8_out);
  not not_8 (not_8_out, a);
  and and_7 (and_7_out, s1_q, s0_q, not_9_out);
  not not_9 (not_9_out, a);
  and and_8 (and_8_out, s0_q, not_10_out);
  not not_10 (not_10_out, a);
  not not_11 (not_11_out, s2_q);
  and and_9 (and_9_out, not_11_out, not_12_out, a);
  not not_12 (not_12_out, s0_q);
  not not_13 (not_13_out, s1_q);
  not not_14 (not_14_out, s0_q);
  and and_10 (and_10_out, not_13_out, not_14_out, a);
  Register #(.width(1)) s0 (.D(or_3_out), .en(in_2), .Q(s0_q), .clk(clock_1_out));  // open: clr
  or or_2 (or_2_out, and_4_out, and_5_out, and_6_out, and_7_out);
  or or_3 (or_3_out, and_8_out, and_9_out, and_10_out);
  not not_15 (not_15_out, s0_q);
  not not_16 (not_16_out, s2_q);
  not not_17 (not_17_out, s2_q);
  not not_18 (not_18_out, s1_q);
  not not_19 (not_19_out, s2_q);
  not not_20 (not_20_out, s1_q);
  not not_21 (not_21_out, s2_q);
  not not_22 (not_22_out, s0_q);
  and and_11 (and_11_out, s1_q, not_15_out);
  and and_12 (and_12_out, s2_q, s0_q);
  and and_13 (and_13_out, not_16_out, s1_q);
  and and_14 (and_14_out, not_17_out, s0_q);
  and and_15 (and_15_out, s2_q, not_18_out);
  and and_16 (and_16_out, not_19_out, not_20_out, s0_q);
  and and_17 (and_17_out, not_21_out, s1_q, not_22_out);
  or or_4 (x, and_11_out, and_12_out);
  or or_5 (y, and_13_out, and_14_out);
  or or_6 (z, and_15_out, and_16_out, and_17_out);
endmodule
