// Logisim project Hw4 circuit.circ as structural Verilog: 1 circuit, main circuit main
module main (
  input  [5:0] in_1,
  input  cl,
  input  ld,
  input  in_4,
  input  sw,
  input  in_6,
  output out_7,
  output out_8,
  output out_9,
  output out_10,
  output out_11,
  output out_12
);

  wire and_1_out, and_2_out, clock_1_out, multiplexer_1_out, multiplexer_2_out, multiplexer_3_out,
       multiplexer_4_out, multiplexer_5_out, multiplexer_6_out, not_1_out, not_2_out, not_3_out;
  wire [1:0] or_2_out;

  not not_1 (not_1_out, cl);
  not not_2 (not_2_out, ld);
  not not_3 (not_3_out, cl);
  and and_1 (and_1_out, not_1_out, not_2_out, sw);
  and and_2 (and_2_out, not_3_out, ld);
  or or_1 (or_2_out[1], and_1_out, cl);
  or or_2 (or_2_out[0], and_2_out, cl);
  Clock clock_1 (.out(clock_1_out));
  Multiplexer #(.select(2)) multiplexer_1 (
    .in0(out_7), .in1(in_1[5]), .in2(out_8), .in3(in_4), .out(multiplexer_1_out), .sel(or_2_out), .en(in_6));
  D_Flip_Flop d_ff_1 (.clk(clock_1_out), .D(multiplexer_1_out), .Q(out_7), .en(in_6));  // open: Qn, preset, reset
  Multiplexer #(.select(2)) multiplexer_2 (
    .in0(out_8), .in1(in_1[4]), .in2(out_7), .in3(in_4), .out(multiplexer_2_out), .sel(or_2_out), .en(in_6));
  D_Flip_Flop d_ff_2 (.clk(clock_1_out), .D(multiplexer_2_out), .Q(out_8), .en(in_6));  // open: Qn, preset, reset
  Multiplexer #(.select(2)) multiplexer_3 (
    .in0(out_9), .in1(in_1[3]), .in2(out_10), .in3(in_4), .out(multiplexer_3_out), .sel(or_2_out), .en(in_6));
  D_Flip_Flop d_ff_3 (.clk(clock_1_out), .D(multiplexer_3_out), .Q(out_9), .en(in_6));  // open: Qn, preset, reset
  Multiplexer #(.select(2)) multiplexer_4 (
    .in0(out_10), .in1(in_1[2]), .in2(out_9), .in3(in_4), .out(multiplexer_4_out), .sel(or_2_out), .en(in_6));
  D_Flip_Flop d_ff_4 (.clk(clock_1_out), .D(multiplexer_4_out), .Q(out_10), .en(in_6));  // open: Qn, preset, reset
  Multiplexer #(.select(2)) multiplexer_5 (
    .in0(out_11), .in1(in_1[1]), .in2(out_12), .in3(in_4), .out(multiplexer_5_out), .sel(or_2_out), .en(in_6));
  D_Flip_Flop d_ff_5 (.clk(clock_1_out), .D(multiplexer_5_out), .Q(out_11), .en(in_6));  // open: Qn, preset, reset
  Multiplexer #(.select(2)) multiplexer_6 (
    .in0(out_12), .in1(in_1[0]), .in2(out_11), .in3(in_4), .out(multiplexer_6_out), .sel(or_2_out), .en(in_6));
  D_Flip_Flop d_ff_6 (.clk(clock_1_out), .D(multiplexer_6_out), .Q(out_12), .en(in_6));  // open: Qn, preset, reset
endmodule
